// Logisim project CPU.circ as structural Verilog: 6 circuits, main circuit CPU
// OpCode
module CPU (
);

  wire CLK, HALT, I_type, multiplexer_1_out, Write;
  wire [3:0] A, A_val, alu_1_value, B, B_Imm, B_val, C, OpCode;
  wire [4:0] adder_1_out, PC_q;

  Adder #(.width(5)) adder_1 (.a(PC_q), .b(5'b00100), .out(adder_1_out));  // open: cin, cout
  Clock clock_1 (.out(CLK));
  HALT_CHECK halt_check_1 (.Instructions(OpCode), .HALT(HALT));
  Counter #(.width(5), .max('h1f)) PC (
    .D(adder_1_out), .Q(PC_q), .clk(multiplexer_1_out));  // open: load, count, carry, clr
  Multiplexer #(.enable("false")) multiplexer_1 (.in0(CLK), .in1(1'b0), .out(multiplexer_1_out), .sel(HALT));
  I_Check i_check_1 (.Instructions(OpCode), .out_2(I_type));
  ROM #(.addrWidth(5), .dataWidth(16)) rom_1 (.addr(PC_q), .data({OpCode, C, A, B_Imm}));  // open: sel
  Reg_File Reg_File (
    .A(A), .B(B_Imm), .C(C), .Data_In(alu_1_value), .Reg_Write(Write), .CLK(CLK), .A_DATA(A_val), .B_DATA(B));
  Multiplexer #(.width(4), .enable("false")) multiplexer_2 (.in0(B), .in1(B_Imm), .out(B_val), .sel(I_type));
  W_Check w_check_1 (.Instructions(OpCode), .A_DATA(Write));
  ALU alu_1 (.Instructions(OpCode), .A(A_val), .B(B_val), .Value(alu_1_value));

  // Notes on the sheet:
  //   PC
  //   Sairamvinay Vijayaraghavan - 913603345
  //   Hariharan Sezhiyan - 913644281
  //   Instructions
  //   contents of rom_1 (hex, n*v repeats v):
  //   2003 2106 1005 3210 4301 5433 6520 763c 8720 986f b938 ca77 db13 ec62 fd85 e05
endmodule

module Reg_File (
  input  [3:0] A,
  input  [3:0] B,
  input  [3:0] C,
  input  [3:0] Data_In,
  input  Reg_Write,
  input  CLK,
  output [3:0] A_DATA,
  output [3:0] B_DATA
);

  wire Write_Reg0, Write_Reg1, Write_Reg2, Write_Reg3, Write_Reg4, Write_Reg5, Write_Reg6, Write_Reg7,
       Write_Reg8, Write_Reg9, Write_Reg10, Write_Reg11, Write_Reg12, Write_Reg13, Write_Reg14, Write_Reg15;
  wire [3:0] Reg0, Reg1, Reg2, Reg3, Reg4, Reg5, Reg6, Reg7, Reg8, Reg9, Reg10, Reg11, Reg12, Reg13, Reg14,
       Reg15;

  Demultiplexer #(.select(4), .enable("false")) demultiplexer_1 (
    .out0(Write_Reg0), .out1(Write_Reg1), .out2(Write_Reg2), .out3(Write_Reg3), .out4(Write_Reg4),
    .out5(Write_Reg5), .out6(Write_Reg6), .out7(Write_Reg7), .out8(Write_Reg8), .out9(Write_Reg9),
    .out10(Write_Reg10), .out11(Write_Reg11), .out12(Write_Reg12), .out13(Write_Reg13), .out14(Write_Reg14),
    .out15(Write_Reg15), .in(Reg_Write), .sel(C));
  // Probe on Reg0
  Register #(.width(4)) u_Reg0 (.D(Data_In), .en(Write_Reg0), .Q(Reg0), .clk(CLK));  // open: clr
  // Probe on Reg4
  Register #(.width(4)) u_Reg4 (.D(Data_In), .en(Write_Reg4), .Q(Reg4), .clk(CLK));  // open: clr
  // Probe on Reg8
  Register #(.width(4)) u_Reg8 (.D(Data_In), .en(Write_Reg8), .Q(Reg8), .clk(CLK));  // open: clr
  // Probe on Reg12
  Register #(.width(4)) u_Reg12 (.D(Data_In), .en(Write_Reg12), .Q(Reg12), .clk(CLK));  // open: clr
  // Probe on Reg1
  Register #(.width(4)) u_Reg1 (.D(Data_In), .en(Write_Reg1), .Q(Reg1), .clk(CLK));  // open: clr
  // Probe on Reg5
  Register #(.width(4)) u_Reg5 (.D(Data_In), .en(Write_Reg5), .Q(Reg5), .clk(CLK));  // open: clr
  // Probe on Reg9
  Register #(.width(4)) u_Reg9 (.D(Data_In), .en(Write_Reg9), .Q(Reg9), .clk(CLK));  // open: clr
  // Probe on Reg13
  Register #(.width(4)) u_Reg13 (.D(Data_In), .en(Write_Reg13), .Q(Reg13), .clk(CLK));  // open: clr
  Register #(.width(4)) u_Reg2 (.D(Data_In), .en(Write_Reg2), .Q(Reg2), .clk(CLK));  // open: clr
  Register #(.width(4)) u_Reg6 (.D(Data_In), .en(Write_Reg6), .Q(Reg6), .clk(CLK));  // open: clr
  Register #(.width(4)) u_Reg10 (.D(Data_In), .en(Write_Reg10), .Q(Reg10), .clk(CLK));  // open: clr
  Register #(.width(4)) u_Reg14 (.D(Data_In), .en(Write_Reg14), .Q(Reg14), .clk(CLK));  // open: clr
  // Probe on Reg2
  // Probe on Reg6
  // Probe on Reg10
  // Probe on Reg14
  // Probe on Reg3
  Register #(.width(4)) u_Reg3 (.D(Data_In), .en(Write_Reg3), .Q(Reg3), .clk(CLK));  // open: clr
  // Probe on Reg7
  Register #(.width(4)) u_Reg7 (.D(Data_In), .en(Write_Reg7), .Q(Reg7), .clk(CLK));  // open: clr
  // Probe on Reg11
  Register #(.width(4)) u_Reg11 (.D(Data_In), .en(Write_Reg11), .Q(Reg11), .clk(CLK));  // open: clr
  // Probe on Reg15
  Register #(.width(4)) u_Reg15 (.D(Data_In), .en(Write_Reg15), .Q(Reg15), .clk(CLK));  // open: clr
  Multiplexer #(.select(4), .width(4), .enable("false")) multiplexer_1 (
    .in0(Reg0), .in1(Reg1), .in2(Reg2), .in3(Reg3), .in4(Reg4), .in5(Reg5), .in6(Reg6), .in7(Reg7),
    .in8(Reg8), .in9(Reg9), .in10(Reg10), .in11(Reg11), .in12(Reg12), .in13(Reg13), .in14(Reg14),
    .in15(Reg15), .out(A_DATA), .sel(A));
  Multiplexer #(.select(4), .width(4), .enable("false")) multiplexer_2 (
    .in0(Reg0), .in1(Reg1), .in2(Reg2), .in3(Reg3), .in4(Reg4), .in5(Reg5), .in6(Reg6), .in7(Reg7),
    .in8(Reg8), .in9(Reg9), .in10(Reg10), .in11(Reg11), .in12(Reg12), .in13(Reg13), .in14(Reg14),
    .in15(Reg15), .out(B_DATA), .sel(B));
endmodule

module ALU (
  input  [3:0] Instructions,
  input  [3:0] A,
  input  [3:0] B,
  output [3:0] Value
);

  wire [3:0] ADD, AND, NEGATE, NOT, OR, SUB, XOR;

  assign AND = A & B;  // AND_Gate and_1, 4 bits wide
  assign OR = A | B;  // OR_Gate or_1, 4 bits wide
  assign XOR = A ^ B;  // XOR_Gate xor_1, 4 bits wide
  assign NOT = ~A;  // NOT_Gate not_1, 4 bits wide
  Negator #(.width(4)) negator_1 (.in(A), .out(NEGATE));
  Subtractor #(.width(4)) subtractor_1 (.a(A), .b(B), .out(SUB));  // open: bin, bout
  Adder #(.width(4)) adder_1 (.a(A), .b(B), .out(ADD));  // open: cin, cout
  Multiplexer #(.select(4), .width(4), .enable("false")) multiplexer_1 (
    .in2(B), .in3(A), .in4(AND), .in5(AND), .in6(OR), .in7(OR), .in8(XOR), .in9(XOR), .in10(NOT),
    .in11(NEGATE), .in12(ADD), .in13(ADD), .in14(SUB), .in15(SUB), .out(Value), .sel(Instructions));  // open: in0, in1

  // Other names for the same wires on the sheet: ALU_Cntrl[3:0] = Instructions
endmodule

module I_Check (
  input  [3:0] Instructions,
  output out_2
);

  wire ADDI, ANDI, decoder_1_out1, decoder_1_out3, decoder_1_out4, decoder_1_out6, decoder_1_out8,
       decoder_1_out10, decoder_1_out11, decoder_1_out12, decoder_1_out14, HALT, LOAD, ORI, SUBI, XORI;

  Decoder #(.select(4)) decoder_1 (
    .out0(HALT), .out1(decoder_1_out1), .out2(LOAD), .out3(decoder_1_out3), .out4(decoder_1_out4),
    .out5(ANDI), .out6(decoder_1_out6), .out7(ORI), .out8(decoder_1_out8), .out9(XORI),
    .out10(decoder_1_out10), .out11(decoder_1_out11), .out12(decoder_1_out12), .out13(ADDI),
    .out14(decoder_1_out14), .out15(SUBI), .sel(Instructions));  // open: en
  or or_1 (out_2, LOAD, ANDI, ORI, XORI, ADDI, SUBI);

  // Other names for the same wires on the sheet: I_type = out_2; OpCode[3:0] = Instructions
endmodule

module W_Check (
  input  [3:0] Instructions,
  output A_DATA
);

  Multiplexer #(.select(4), .enable("false")) multiplexer_1 (
    .in0(1'b0), .in1(1'b0), .in2(1'b1), .in3(1'b1), .in4(1'b1), .in5(1'b1), .in6(1'b1), .in7(1'b1),
    .in8(1'b1), .in9(1'b1), .in10(1'b1), .in11(1'b1), .in12(1'b1), .in13(1'b1), .in14(1'b1), .in15(1'b1),
    .out(A_DATA), .sel(Instructions));

  // Other names for the same wires on the sheet: OpCode[3:0] = Instructions
endmodule

module HALT_CHECK (
  input  [3:0] Instructions,
  output HALT
);

  Decoder #(.select(4)) decoder_1 (
    .out0(HALT), .sel(Instructions));  // open: out1, out2, out3, out4, out5, out6, out7, out8, out9, out10, out11, out12, out13, out14, out15, en

  // Other names for the same wires on the sheet: ALU_Cntrl[3:0] = Instructions
endmodule
